// Logisim project 3display7segmentos.circ as structural Verilog: 1 circuit, main circuit main
module main (
  input  in_1,
  input  in_2,
  input  in_3,
  input  in_4,
  input  in_5,
  input  in_6,
  input  in_7,
  input  in_8,
  input  in_9,
  input  in_10,
  input  in_11,
  input  in_12,
  input  in_13,
  input  in_14,
  input  in_15,
  input  in_16,
  input  in_17,
  input  in_18,
  input  in_19,
  input  in_20,
  input  in_21,
  output out_22,
  output out_23,
  output out_24,
  output out_25,
  output COUNTER_2_BITS,
  output out_27,
  output out_28,
  output out_29,
  output out_30,
  output out_31,
  output out_32,
  output out_33,
  output out_34
);

  wire A, A_prime, AND1, AND2, AND3, AND4, AND5, AND6, AND7, AND8, AND9, B, B_prime, C, C_prime, CLK, D,
       D_prime, not_5_out, not_6_out, not_7_out, not_8_out, OD, Q0_prime, Q1_prime;

  Clock clock_1 (.out(CLK));
  J_K_Flip_Flop j_k_ff_1 (
    .J(1'b1), .clk(CLK), .K(1'b1), .Q(out_27), .Qn(Q0_prime), .en(1'b1), .reset(in_21));  // open: preset
  not not_1 (A_prime, A);
  not not_2 (B_prime, B);
  not not_3 (C_prime, C);
  not not_4 (D_prime, D);
  J_K_Flip_Flop j_k_ff_2 (
    .J(out_27), .clk(CLK), .K(out_27), .Q(COUNTER_2_BITS), .Qn(Q1_prime), .en(1'b1));  // open: preset, reset
  and and_1 (AND1, B, D);
  and and_2 (AND2, B_prime, D_prime);
  and and_3 (AND3, C, D);
  and and_4 (AND4, C_prime, D_prime);
  Multiplexer #(.select(2), .enable("false")) multiplexer_1 (
    .in0(in_16), .in1(in_12), .in2(in_8), .in3(in_4), .out(D), .sel({COUNTER_2_BITS, out_27}));
  and and_5 (AND5, C, D_prime);
  and and_6 (AND6, B_prime, C);
  and and_7 (AND7, B, C_prime, D);
  and and_8 (AND8, B, C_prime);
  and and_9 (AND9, B, D_prime);
  not not_5 (not_5_out, out_27);
  not not_6 (not_6_out, COUNTER_2_BITS);
  not not_7 (not_7_out, out_27);
  and and_10 (out_25, not_5_out, not_6_out);
  and and_11 (out_23, not_7_out, COUNTER_2_BITS);
  Multiplexer #(.select(2), .enable("false")) multiplexer_2 (
    .in0(in_15), .in1(in_11), .in2(in_7), .in3(in_3), .out(C), .sel({COUNTER_2_BITS, out_27}));
  or or_1 (out_28, A, AND1, AND2, C);
  or or_2 (out_29, AND4, AND3, B_prime);
  or or_3 (out_30, B, D, C_prime);
  and and_12 (out_24, out_27, not_8_out);
  not not_8 (not_8_out, COUNTER_2_BITS);
  and and_13 (out_22, out_27, COUNTER_2_BITS);
  Multiplexer #(.select(2), .enable("false")) multiplexer_3 (
    .in0(in_14), .in1(in_10), .in2(in_6), .in3(in_2), .out(B), .sel({COUNTER_2_BITS, out_27}));
  or or_4 (out_31, A, AND2, AND5, AND6, AND7);
  or or_5 (out_32, AND2, AND5);
  or or_6 (out_33, A, AND4, AND9, AND8);
  _7_Segment_Display u_7_segment_display_1 (
    .g(out_34), .f(out_33), .a(out_28), .b(out_29), .e(out_32), .d(out_31), .c(out_30), .dp(OD));
  Multiplexer #(.select(2), .enable("false")) multiplexer_4 (
    .in0(in_13), .in1(in_9), .in2(in_5), .in3(in_1), .out(A), .sel({COUNTER_2_BITS, out_27}));
  or or_7 (out_34, A, AND6, AND5, AND8);
  Multiplexer #(.select(2), .enable("false")) multiplexer_5 (
    .in0(in_20), .in1(in_19), .in2(in_18), .in3(in_17), .out(OD), .sel({COUNTER_2_BITS, out_27}));

  // Other names for the same wires on the sheet: Q0 = out_27; Q1 = COUNTER_2_BITS; a_t = out_28; b_t = out_29;
  //   c_t = out_30; D0 = in_20; D1 = in_19; D2 = in_18; D3 = in_17; d_t = out_31; e = out_32; e0 = out_25;
  //   e1 = out_24; e2 = out_23; e3 = out_22; f = out_33; g = out_34; I0 = in_16; I1 = in_15; I2 = in_14; I3 = in_13;
  //   I4 = in_12; I5 = in_11; I6 = in_10; I7 = in_9; I8 = in_8; I9 = in_7; I10 = in_6; I11 = in_5; I12 = in_4;
  //   I13 = in_3; I14 = in_2; I15 = in_1; O0 = A; O1 = B; O2 = C; O3 = D

  // Notes on the sheet:
  //   INPUTS
  //   DECODER
  //   ENABLE DISPLAY
  //   MUX4:1, CHOOSE 4 BITS
  //   OUTPUTS
endmodule
